# Fritzing sketch rpi-pico-relay (saved by Fritzing 1.0.0rc)
breadboards: 1

parts:
  Mod1 = Raspberry Pi Pico
  relay = QIANJI relay [part_number=JQC-3F]
  maintenance-rocker-switch = SWITCH-SPST-2 [package=switch-spst-vertical]
  output-usb-device = USB Connectors [package=usb-a-s-nosilk-female]
  input-usb-device = Adafruit USB Type C Breakout [part_number=4090]
  input-rpi-pico = Adafruit USB Type C Breakout [part_number=4090]

nets:
  N1: Mod1.pin_1, relay.DC2
  N2: Mod1.pin_2, maintenance-rocker-switch.P
  GND: Mod1.pin_3, Mod1.pin_8, Mod1.pin_13, Mod1.pin_18, Mod1.pin_23, Mod1.pin_28, Mod1.pin_33, Mod1.pin_38, relay.DC1, input-usb-device.GND, input-rpi-pico.GND
  N3: Mod1.pin_40, relay.COMMON, maintenance-rocker-switch.O, input-rpi-pico.VBUS
  N4: relay.NO, output-usb-device.GND
  N5: output-usb-device.VBUS, input-usb-device.VBUS

custom parts:
  Raspberry Pi Pico: Raspberry Pi Pico. Based around the RP2040 microcontroller the Pico is a low cost microcontroller device bringing Raspberry Pi quality, cost, and easy of use to the microcontroller space. Jan 2021, Split part in to two versions: tht (this one) and SMD. This one will drill holes for a .1 in header in pcb to allow plugging in the module as well as providing pads to solder the module to the top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
  QIANJI relay: QIANJI JQC-3F, adjusted pins
  Adafruit USB Type C Breakout: Adafruit breakout board for USB Type C socket.

// code stored in the sketch: Untitled.bas

